# Fritzing sketch CookieJar BigBreadBoard (saved by Fritzing 1.0.1rc)
breadboards: 3

parts:
  Breadboard4 = Breadboard Split Power
  Breadboard5 = Breadboard Split Power
  A1 = Particle - Photon2
  Part1 = 4x4 Keypad [part_number=101207]
  OLED_I2C1 = OLED 128x64 I2C Monochrome Display
  Neopixel1 = Adafruit RBG Smart Neopixel [package="DIP (Dual Inline) [THT]"]
  Neopixel2 = Adafruit RBG Smart Neopixel [package="DIP (Dual Inline) [THT]"]
  Neopixel3 = Adafruit RBG Smart Neopixel [package="DIP (Dual Inline) [THT]"]
  Neopixel4 = Adafruit RBG Smart Neopixel [package="DIP (Dual Inline) [THT]"]
  Neopixel5 = Adafruit RBG Smart Neopixel [package="DIP (Dual Inline) [THT]"]
  J1 = Basic Servo
  Part2 = HC-SR501 Body Sensor Module

nets:
  N1: Breadboard4.pin15Y, Breadboard4.pin17Y, Breadboard4.pin29Y, Breadboard5.pin3Y, Breadboard5.pin15Y, Breadboard5.pin17Y
  GND: Breadboard4.pin20Z, Breadboard4.pin29Z, Breadboard5.pin3Z, Breadboard5.pin11Z, OLED_I2C1.GND, Neopixel1.G, Neopixel2.G, Neopixel4.G, Neopixel5.G, Part2.GND
  3.3V: A1.Pin_2, A1.Pin_31, OLED_I2C1.VDD, J1.vcc
  N2: A1.Pin_7, J1.pulse
  N3: A1.Pin_8, Part1.8
  N4: A1.Pin_9, Part1.7
  N5: A1.Pin_10, Part1.6
  N6: A1.Pin_11, Part1.5
  N7: A1.Pin_12, Part1.4
  N8: A1.Pin_13, Part1.3
  N9: A1.Pin_14, Part1.2
  N10: A1.Pin_15, Part1.1
  N11: A1.Pin_17, OLED_I2C1.SDA
  N12: A1.Pin_18, OLED_I2C1.SCK
  N13: A1.Pin_19, Neopixel1.In
  N14: A1.Pin_21, Part2.OUT
  5V: Neopixel1.+, Neopixel2.+, Neopixel3.+, Neopixel5.+, Part2.VCC
  N15: Neopixel1.O, Neopixel2.In
  N16: Neopixel2.O, Neopixel3.In
  N17: Neopixel3.O, Neopixel4.In
  N18: Neopixel4.O, Neopixel5.In

custom parts:
  Breadboard Split Power: A custom 6 pin per group power supply strip where the top row (ground) is all bussed together and the bottom row (+V) is split in two groups of 12 pins. This version is modified to be a loadable part and was rescaled to be on the standard 1px = 1thou grid with the size set in inches
  Particle - Photon2: The Photon 2 is a microcontroller and Wi-Fi networking developed by particle. Features: 802.11a/b/g/n Wi-Fi, 2.4 GHz and 5 GHz Integrated PCB antenna Integrated U.FL connector for external antenna Integrated RF switch BLE 5 using same antenna as Wi-Fi Realtek RTL8721DM MCU ARM Cortex M33 CPU, 200 MHz 2048 KB (2 MB) user application maximum size 3072 KB (3 MB) of RAM available to user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
  4x4 Keypad: Matrix membrane keypad 4x4
  HC-SR501 Body Sensor Module: Pyroelectric Infrared PIR Motion Sensor Detector Module
